// Logisim project bfcpu.circ as structural Verilog: 2 circuits, main circuit main
module main (
);

  wire and_1_out, and_2_out, and_3_out, clock_1_out, decoder_1_out1, decoder_1_out2, decoder_1_out3,
       not_1_out, t_ff_1_q, t_ff_1_qn, t_ff_2_q;
  wire [1:0] multiplexer_1_out;
  wire [3:0] rom_1_data;
  wire [3:2] multiplexer_1_out_2;
  wire [7:0] BUF_q, BUF_q_2, controlled_buffer_1_out, counter_1_q;
  wire [15:0] alu_1_x_prime, DP_q, multiplexer_2_out, PC_q;

  and and_1 (and_1_out, decoder_1_out1, t_ff_1_qn);
  Register #(.width(16), .trigger("rising")) PC (
    .D({BUF_q_2, BUF_q}), .en(1'b1), .Q(PC_q), .clk(and_1_out), .clr(1'b0));
  Decoder #(.select(2), .tristate("false")) decoder_1 (
    .out1(decoder_1_out1), .out2(decoder_1_out2), .out3(decoder_1_out3), .sel(multiplexer_1_out));  // open: out0
  ROM #(.addrWidth(16), .dataWidth(4)) rom_1 (.addr(PC_q), .data(rom_1_data));  // open: sel
  Clock #(.highDuration(1), .lowDuration(1)) clock_1 (.out(clock_1_out));
  T_Flip_Flop #(.trigger("rising")) t_ff_1 (
    .clk(clock_1_out), .T(1'b1), .Q(t_ff_1_q), .Qn(t_ff_1_qn));  // open: preset, reset, en
  // Probe on counter_1_q
  Counter #(.width(8), .max('hff), .ongoal("wrap"), .trigger("rising")) counter_1 (
    .Q(counter_1_q), .clk(clock_1_out));  // open: load, D, count, carry, clr
  Register #(.width(16), .trigger("rising")) DP (
    .D({BUF_q_2, BUF_q}), .en(1'b1), .Q(DP_q), .clk(and_2_out), .clr(1'b0));
  and and_2 (and_2_out, decoder_1_out2, t_ff_1_qn);
  T_Flip_Flop #(.trigger("rising")) t_ff_2 (.clk(t_ff_1_qn), .T(1'b1), .Q(t_ff_2_q));  // open: Qn, preset, reset, en
  Multiplexer #(.select(1), .width(4)) multiplexer_1 (
    .in0(rom_1_data), .in1(4'b0001), .out({multiplexer_1_out_2, multiplexer_1_out}), .sel(t_ff_2_q));
  and and_3 (and_3_out, decoder_1_out3, t_ff_1_qn);
  // Probe on multiplexer_1_out
  not not_1 (not_1_out, and_3_out);
  Multiplexer #(.select(2), .width(16)) multiplexer_2 (
    .in1(DP_q), .in2(PC_q), .in3({{8{1'b0}}, controlled_buffer_1_out}), .out(multiplexer_2_out),
    .sel(multiplexer_1_out));  // open: in0
  assign controlled_buffer_1_out = and_3_out ? BUF_q : 8'bz;  // Controlled_Buffer controlled_buffer_1
  RAM #(.addrWidth(16), .dataWidth(8), .bus("asynch")) ram_1 (
    .addr(DP_q), .data(controlled_buffer_1_out), .sel(1'b1), .ld(not_1_out), .clr(1'b0));
  // Probe on alu_1_x_prime
  ALU alu_1 (.x(multiplexer_2_out), .m(multiplexer_1_out_2[3]), .x_prime(alu_1_x_prime));
  // Probe on {BUF_q_2, BUF_q}
  Register #(.width(16), .trigger("rising")) BUF (
    .D(alu_1_x_prime), .Q({BUF_q_2, BUF_q}), .clk(t_ff_1_q), .clr(1'b0));  // open: en

  // Notes on the sheet:
  //   PROGRAM ROM
  //   contents of rom_1 (hex, n*v repeats v):
  //   3 2 3 2 a
  //   CONTROL UNIT
  //   selOperand
  //   fDec
  //   DATA RAM
endmodule

module ALU (
  input  [15:0] x,
  input  m,
  output [15:0] x_prime
);

  wire adder_1_cout, adder_2_cout, adder_3_cout;

  Adder #(.width(4)) adder_1 (.a(x[3:0]), .b({{3{m}}, 1'b1}), .out(x_prime[3:0]), .cin(1'b0), .cout(adder_1_cout));
  Adder #(.width(4)) adder_2 (.a(x[7:4]), .b({4{m}}), .out(x_prime[7:4]), .cin(adder_1_cout), .cout(adder_2_cout));
  Adder #(.width(4)) adder_3 (.a(x[11:8]), .b({4{m}}), .out(x_prime[11:8]), .cin(adder_2_cout), .cout(adder_3_cout));
  Adder #(.width(4)) adder_4 (.a(x[15:12]), .b({4{m}}), .out(x_prime[15:12]), .cin(adder_3_cout));  // open: cout
endmodule
